# Fritzing sketch electronic_circuit (saved by Fritzing 1.0.1rc)
circuit board: 8.46667cm x 5.64444cm
breadboards: 2

parts:
  M1 = DOIT Esp32 DevKit v1 (30 pins long, 11 pins width) [part_number=ESP32S-PIN30]
  Motor_Right = Adafruit DRV8871 [part_number=01]
  Motor_Left = Adafruit DRV8871 [part_number=02]
  Motor_Top = Adafruit DRV8871 [part_number=03]
  Joystick_1 = Thumb Joystick
  Joystick_2 = Thumb Joystick
  Motor_Top_2 = DC Motor [voltage_(max)=6V voltage_(min)=3V]
  Motor_Left_2 = DC Motor [voltage_(max)=6V voltage_(min)=3V]
  Motor_Right_2 = DC Motor [voltage_(max)=6V voltage_(min)=3V]
  Power_Regulator_12V = Boost Convertor [part_number=XL6009E1 package=THT]
  Power_Regulator_5V = Boost Convertor [part_number=XL6009E1 package=THT]

nets:
  VCC: M1.3V3, Joystick_1.VCC, Joystick_2.VCC
  GND: M1.GND, Motor_Right.GND, Motor_Left.GND, Motor_Top.GND, Joystick_1.GND, Joystick_2.GND, Power_Regulator_12V.Negative_Output, Power_Regulator_5V.Negative_Output
  N1: M1.VN, Joystick_1.VERT
  N2: M1.D34, Joystick_2.HORZ
  N3: M1.D35, Joystick_2.VERT
  N4: M1.D32, Motor_Left.IN1
  N5: M1.D33, Motor_Left.IN2
  N6: M1.D25, Motor_Right.IN1
  N7: M1.D26, Motor_Right.IN2
  N8: M1.D14, Motor_Top.IN2
  N9: M1.D13, Motor_Top.IN1
  N10: M1.VIN, Power_Regulator_5V.Positive_Output
  N11: Motor_Right.VMOTOR, Motor_Left.VMOTOR, Motor_Top.VMOTOR, Power_Regulator_12V.Positive_Output
  N12: Motor_Right.OUT2, Motor_Right_2.pin_1
  N13: Motor_Right.OUT1, Motor_Right_2.pin_2
  N14: Motor_Left.OUT2, Motor_Left_2.pin_1
  N15: Motor_Left.OUT1, Motor_Left_2.pin_2
  N16: Motor_Top.OUT2, Motor_Top_2.pin_1
  N17: Motor_Top.OUT1, Motor_Top_2.pin_2

custom parts:
  DOIT Esp32 DevKit v1 (30 pins long, 11 pins width): The DOIT Esp32 DevKit v1 is one of the development board created by DOIT to evaluate the ESP-WROOM-32 module. It is based on the ESP32 microcontroller that boasts Wifi, Bluetooth, Ethernet and Low Power support all in a single chip. (vanepp) made breadboard work, adjusted pin numbering and labels and reduced size of schematic and cleaned up pcb. This chip is 30pins long (2 x15) and 11 pins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
  Adafruit DRV8871: Crank up your robotics with powerful Adafruit DRV8871 motor driver breakout board. This motor driver has a lot of great specs that make it useful for a wide variety of mechatronics. In particular, the simple resistor-set current limiting and auto-magic PWM support make it super easy to use. Check out the specs for the DRV8871: 6.5V to 45V motor power voltage Up to 5.5V logic level on IN pins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
  Boost Convertor: DC to DC boost convertor
